// Logisim project CPU.circ as structural Verilog: 2 circuits, main circuit RegisterBank
module RegisterBank (
  input  [15:0] DATA_IN,
  input  [2:0] in_2,
  input  READ_ENABLE,
  input  [2:0] in_4,
  input  WRITE_ENABLE,
  output [15:0] Data_Out
);

  wire clock_1_out, not_1_out;
  wire [7:0] decoder_1_out0;
  wire [15:0] controlled_buffer_1_out, Reg0_q, Reg1_q, Reg2_q, Reg3_q, Reg4_q, Reg5_q, Reg6_q, Reg7_q;

  Pull_Resistor pull_resistor_1 (.node(WRITE_ENABLE));
  Decoder #(.select(3), .disabled(0)) decoder_1 (
    .out0(decoder_1_out0[0]), .out1(decoder_1_out0[1]), .out2(decoder_1_out0[2]), .out3(decoder_1_out0[3]),
    .out4(decoder_1_out0[4]), .out5(decoder_1_out0[5]), .out6(decoder_1_out0[6]), .out7(decoder_1_out0[7]),
    .sel(in_4), .en(WRITE_ENABLE));
  DotMatrix #(.inputtype("row"), .matrixcols(8), .matrixrows(1), .dotshape("circle")) dotmatrix_1 (.row0(decoder_1_out0));
  Clock clock_1 (.out(clock_1_out));
  not not_1 (not_1_out, READ_ENABLE);
  assign controlled_buffer_1_out = not_1_out ? DATA_IN : 16'bz;  // Controlled_Buffer controlled_buffer_1
  Register #(.width(16)) Reg0 (
    .D(controlled_buffer_1_out), .en(decoder_1_out0[0]), .Q(Reg0_q), .clk(clock_1_out));  // open: clr
  Register #(.width(16)) Reg1 (
    .D(controlled_buffer_1_out), .en(decoder_1_out0[1]), .Q(Reg1_q), .clk(clock_1_out));  // open: clr
  Register #(.width(16)) Reg2 (
    .D(controlled_buffer_1_out), .en(decoder_1_out0[2]), .Q(Reg2_q), .clk(clock_1_out));  // open: clr
  Register #(.width(16)) Reg3 (
    .D(controlled_buffer_1_out), .en(decoder_1_out0[3]), .Q(Reg3_q), .clk(clock_1_out));  // open: clr
  Register #(.width(16)) Reg4 (
    .D(controlled_buffer_1_out), .en(decoder_1_out0[4]), .Q(Reg4_q), .clk(clock_1_out));  // open: clr
  Register #(.width(16)) Reg5 (
    .D(controlled_buffer_1_out), .en(decoder_1_out0[5]), .Q(Reg5_q), .clk(clock_1_out));  // open: clr
  Register #(.width(16)) Reg6 (
    .D(controlled_buffer_1_out), .en(decoder_1_out0[6]), .Q(Reg6_q), .clk(clock_1_out));  // open: clr
  Register #(.width(16)) Reg7 (
    .D(controlled_buffer_1_out), .en(decoder_1_out0[7]), .Q(Reg7_q), .clk(clock_1_out));  // open: clr
  assign controlled_buffer_1_out = Data_Out;  // Buffer buffer_1, 16 bits wide
  Pull_Resistor pull_resistor_2 (.node(READ_ENABLE));
  Multiplexer #(.select(3), .width(16)) multiplexer_1 (
    .in0(Reg0_q), .in1(Reg1_q), .in2(Reg2_q), .in3(Reg3_q), .in4(Reg4_q), .in5(Reg5_q), .in6(Reg6_q),
    .in7(Reg7_q), .out(Data_Out), .sel(in_2), .en(READ_ENABLE));

  // Notes on the sheet:
  //   DATA_IN: pull=down
  //   in_4: pull=down
  //   in_2: pull=down
endmodule

module ALU (
  input  [1:0] OPCODE_IN,
  input  READ_ENABLE,
  input  [15:0] DATA_IN,
  input  WRITE_ENABLE,
  input  ADDR,
  output [15:0] DATA_OUT,
  output REGA___REGB,
  output REGA___REGB_2,
  output REGA___REGB_3
);

  wire clock_1_out, decoder_1_out0, decoder_1_out1;
  wire [15:0] adder_1_out, nor_1_out, RegA_q, RegB_q, subtractor_1_out;

  Decoder #(.disabled(0)) decoder_1 (.out0(decoder_1_out0), .out1(decoder_1_out1), .sel(ADDR), .en(WRITE_ENABLE));
  Register #(.width(16)) RegA (.D(DATA_IN), .en(decoder_1_out0), .Q(RegA_q), .clk(clock_1_out));  // open: clr
  Clock clock_1 (.out(clock_1_out));
  Register #(.width(16)) RegB (.D(DATA_IN), .en(decoder_1_out1), .Q(RegB_q), .clk(clock_1_out));  // open: clr
  Adder #(.width(16)) adder_1 (.a(RegA_q), .b(RegB_q), .out(adder_1_out));  // open: cin, cout
  Subtractor #(.width(16)) subtractor_1 (.a(RegA_q), .b(RegB_q), .out(subtractor_1_out));  // open: bin, bout
  assign nor_1_out = ~(RegA_q | RegB_q);  // NOR_Gate nor_1, 16 bits wide
  Comparator #(.width(16)) comparator_1 (
    .a(RegA_q), .b(RegB_q), .gt(REGA___REGB), .eq(REGA___REGB_2), .lt(REGA___REGB_3));
  Multiplexer #(.select(2), .width(16)) multiplexer_1 (
    .in0(adder_1_out), .in1(subtractor_1_out), .in2(nor_1_out), .out(DATA_OUT), .sel(OPCODE_IN),
    .en(READ_ENABLE));  // open: in3

  // Notes on the sheet:
  //   REGA___REGB_2: pull=down
  //   REGA___REGB_3: pull=down
  //   DATA_IN: pull=down
  //   REGA___REGB: pull=down
endmodule
